# Fritzing sketch bicigenerador (saved by Fritzing 0.8.3b)
circuit board: 7.84989cm x 6.29613cm
breadboards: 1

parts:
  Arduino = Arduino Uno (Rev3)
  RF_-_TX = RF Transmitter [package=THT]
  R3 = Resistor [tolerance=±5% resistance=220 package=THT]
  R4 = Resistor [tolerance=±5% resistance=220 package=THT]
  R5 = Resistor [tolerance=±5% resistance=220 package=THT]
  LED1 = RGB LED (com. anode, rbg) [package="5 mm [THT]"]
  R6 = Resistor [tolerance=±5% resistance=1k package=THT]
  Q2 = NPN-Transistor [part_number=2N2222 package="TO92 [THT]"]
  R7 = Resistor [tolerance=±5% resistance=1k package=THT]
  Q3 = NPN-Transistor [part_number=2N2222 package="TO92 [THT]"]
  R8 = Resistor [tolerance=±5% resistance=10k package=THT]
  GP2Y = screw terminal, 3 pins
  hal = screw terminal, 3 pins
  carga = screw terminal, 2 pins
  mecanico = screw terminal, 2 pins
  D1 = Rectifier Diode [part_number=1N4001 package="300 mil [THT]"]
  D2 = Rectifier Diode [part_number=1N4001 package="300 mil [THT]"]

nets:
  N1: Arduino.A0, GP2Y.pin3
  N2: Arduino.GND, RF_-_TX.pin1, Q2.E, Q3.E, GP2Y.pin1, hal.pin2
  N3: Arduino.D8, R6.Pin_1
  N4: Arduino.D2, R8.Pin_1, hal.pin3
  N5: Arduino.D3_PWM, R3.Pin_0
  N6: Arduino.D4, RF_-_TX.pin2
  N7: Arduino.D5_PWM, R5.Pin_0
  N8: Arduino.D6_PWM, R4.Pin_0
  N9: Arduino.D7, R7.Pin_1
  N10: Arduino.5V, RF_-_TX.pin3, LED1.common_anode, R8.Pin_0, GP2Y.pin2, hal.pin1
  N11: Arduino.VIN, carga.pin1, mecanico.pin1, D1.cathode, D2.cathode
  N12: R3.Pin_1, LED1.red_cathode
  N13: R4.Pin_1, LED1.blue_cathode
  N14: R5.Pin_1, LED1.green_cathode
  N15: R6.Pin_0, Q2.B
  N16: Q2.C, mecanico.pin2, D2.anode
  N17: R7.Pin_0, Q3.B
  N18: Q3.C, carga.pin2, D1.anode

notes:
  Antena
  Data
  +
  R
  G
  B
  Bicigenerador
  Luz & Fuerza
  2013
  Sobre los relays
  http://www.mp3car.com/showwiki.php?title=Relays
  pines 30 - 87 [circuito a controlar]
  pin 85 [gnd]
  pin 86 [control +12]
  12v
  5v
  gnd
  out
  pwr
  Relay Pin 7 > Carga Bateria
  Relay Pin 8 > Negativo

custom parts:
  RF Transmitter: Transmitter for RWS 371 receiver
