# Fritzing sketch frankitropo (saved by Fritzing 0.8.3b)
circuit board: 7.69708cm x 6.47659cm
breadboards: 1

parts:
  RF_-_RX = RWS-371 [package=THT]
  Arduino = Arduino Uno (Rev3)
  Potenciometro_1m = Rotary Potentiometer (Large) [maximum_resistance=100kΩ package=THT]
  11-12 = screw terminal, 2 pins
  9-10 = screw terminal, 2 pins
  7-8 = screw terminal, 2 pins
  5-6 = screw terminal, 2 pins
  3-4 = screw terminal, 2 pins
  2-1 = screw terminal, 2 pins
  R2 = Resistor [tolerance=±5% resistance=10 package=THT]
  REF_GND = screw terminal, 2 pins

nets:
  N1: RF_-_RX.pin1, RF_-_RX.pin_6, RF_-_RX.pin_7, Arduino.GND, Potenciometro_1m.leg1, R2.Pin_0
  N2: RF_-_RX.pin2, Arduino.D1/TX
  N3: RF_-_RX.pin_4, RF_-_RX.pin_5, Arduino.5V, Potenciometro_1m.leg2
  N4: Arduino.A0, Potenciometro_1m.wiper
  N5: Arduino.D8, 7-8.pin2
  N6: Arduino.D9_PWM, 7-8.pin1
  N7: Arduino.D10_PWM/SS, 9-10.pin2
  N8: Arduino.D11_PWM/MOSI, 9-10.pin1
  N9: Arduino.D12/MISO, 11-12.pin2
  N10: Arduino.D13/SCK, 11-12.pin1
  N11: Arduino.D2, 2-1.pin2
  N12: Arduino.D3_PWM, 2-1.pin1
  N13: Arduino.D4, 3-4.pin2
  N14: Arduino.D5_PWM, 3-4.pin1
  N15: Arduino.D6_PWM, 5-6.pin2
  N16: Arduino.D7, 5-6.pin1
  N17: R2.Pin_1, REF_GND.pin1, REF_GND.pin2

notes:
  Luz & Fuerza
  frankitropo
  3-4
  5-6
  7-8
  9-10
  11-12
  receiver
  antenna
  pot
  1-2
  REF GND
  2013
  +
  -
  Frankitropo

custom parts:
  RWS-371: RF Receiver
