# Fritzing sketch mar (saved by Fritzing 0.8.3b)
circuit board: 10.16cm x 5.36194cm
breadboards: 1

parts:
  J1 = screw terminal, 2 pins
  J3 = screw terminal, 2 pins
  J4 = screw terminal, 2 pins
  J2 = screw terminal, 2 pins
  U1 = RWS-371 [package=THT]
  Parte1 = Arduino Mega 2560 (Rev3)
  R1 = Resistor [tolerance=±5% resistance=10 package=THT]
  J5 = screw terminal, 2 pins

nets:
  N1: J1.pin1, Parte1.D2_PWM
  N2: J1.pin2, Parte1.D3_PWM
  N3: J3.pin1, Parte1.D6_PWM
  N4: J3.pin2, Parte1.D7_PWM
  N5: J4.pin1, Parte1.D8_PWM
  N6: J4.pin2, Parte1.D9_PWM
  N7: J2.pin1, Parte1.D4_PWM
  N8: J2.pin2, Parte1.D5_PWM
  N9: U1.pin1, U1.pin_6, U1.pin_7, Parte1.GND, R1.Pin_0
  N10: U1.pin2, Parte1.D22
  N11: U1.pin_4, U1.pin_5, Parte1.5V
  N12: R1.Pin_1, J5.pin1, J5.pin2

notes:
  Mar
  Luz & Fuerza
  2013
  1-2
  3-4
  5-6
  7-8
  REF
  GND
  2-1
  4-3
  6-5
  8-7
  RF - RX
  antenna

custom parts:
  RWS-371: RF Receiver
