# Fritzing sketch rf-test (saved by Fritzing 0.8.3b)
circuit board: 7.23628cm x 5.69846cm
breadboards: 1

parts:
  Arduino = Arduino Uno (Rev3)
  RF_-_TX = RF Transmitter [package=THT]
  R1 = Rotary Potentiometer (Large) [package=THT]

nets:
  N1: Arduino.A0, R1.wiper
  N2: Arduino.GND, RF_-_TX.pin3, R1.leg1
  N3: Arduino.D4, RF_-_TX.pin2
  N4: Arduino.5V, RF_-_TX.pin1, R1.leg2

notes:
  Antena
  +
  R
  G
  B
  Luz & Fuerza
  2013
  RF - RX
  antenna

custom parts:
  RF Transmitter: Transmitter for RWS 371 receiver
